# Fritzing sketch piste (saved by Fritzing 0.9.4)
breadboards: 1

parts:
  Composant1 = Arduino Nano (Rev3.0)
  AU1 = Toggle Switch [package=THT]
  AU2 = Toggle Switch [package=THT]
  AU3 = Toggle Switch [package=THT]
  AU4 = Toggle Switch [package=THT]
  x12 = SMD RGB LED (WS2812) [package=5050]
  U1 = RELAY [package=relay-g5q]
  U2 = RELAY [package=relay-g5q]
  J1 = Screw terminal - 2 pins [package=THT]
  J2 = Screw terminal - 2 pins [package=THT]
  S1 = Pushbutton [package=THT]
  S2 = Pushbutton [package=THT]
  S3 = Pushbutton [package=THT]
  S4 = Pushbutton [package=THT]

nets:
  TX PC: Composant1.D1/TX
  RX PC: Composant1.D0/RX
  GND: Composant1.GND, AU4.L1, x12.VSS, U1.COIL2, U2.COIL2, S4.leg1
  relais: Composant1.D4, U1.COIL1, U2.COIL1
  AU: Composant1.D5, AU1.COM
  WS: Composant1.D6, x12.DIn
  SW: Composant1.D7, S1.leg0
  5V: Composant1.5V, x12.VCC, x12.VDD
  N1: AU1.L1, AU2.COM
  N2: AU2.L1, AU3.COM
  N3: AU3.L1, AU4.COM
  N4: U1.MAIN, J2.pin2
  N5: U1.NC, J2.pin1
  N6: U2.MAIN, J1.pin2
  N7: U2.NC, J1.pin1
  N8: S1.leg1, S2.leg0
  N9: S2.leg1, S3.leg0
  N10: S3.leg1, S4.leg0

notes:
  6 GO
  1-5 feux départ
  7 Stop
  8 Jaune
  Alim / DAVIC
  PcLapCounter
